# Fritzing sketch krets (saved by Fritzing 0.9.6b)
breadboards: 1

parts:
  Part2 = Arduino Nano (Rev3.0) (ICSP)
  LED1 = smd LED [color="Blue (525nm)" package="0603 [SMD]"]
  LED2 = smd LED [color="Green (570nm)" package="0603 [SMD]"]
  LED3 = smd LED [color="Red (633nm)" package="0603 [SMD]"]
  LED4 = smd LED [color="Yellow (595nm)" package="0603 [SMD]"]
  S1 = Pushbutton [package="[THT]"]
  S2 = Pushbutton [package="[THT]"]
  S3 = Pushbutton [package="[THT]"]
  S4 = Pushbutton [package="[THT]"]
  R1 = Resistor [tolerance=±5% power=0.25 resistance=100k package=THT]
  R2 = Resistor [tolerance=±5% power=0.25 resistance=100k package=THT]
  R3 = Resistor [tolerance=±5% power=0.25 resistance=100k package=THT]
  R4 = Resistor [tolerance=±5% power=0.25 resistance=100k package=THT]
  R5 = Resistor [tolerance=±5% power=0.25 resistance=220 package=THT]
  R6 = Resistor [tolerance=±5% power=0.25 resistance=220 package=THT]
  R7 = Resistor [tolerance=±5% power=0.25 resistance=220 package=THT]
  R8 = Resistor [tolerance=±5% power=0.25 resistance=220 package=THT]

nets:
  N1: Part2.D5, S4.Pin_3, S4.Pin_4, R4.Pin_0
  N2: Part2.D6, S3.Pin_3, S3.Pin_4, R3.Pin_0
  N3: Part2.D7, S2.Pin_3, S2.Pin_4, R2.Pin_0
  N4: Part2.D8, S1.Pin_3, S1.Pin_4, R1.Pin_1
  N5: Part2.D9, LED4.cathode, R8.Pin_0, R8.Pin_1
  N6: Part2.D10, LED3.cathode, R7.Pin_0, R7.Pin_1
  N7: Part2.D11/MOSI, LED2.cathode, R6.Pin_0, R6.Pin_1
  N8: Part2.D12/MISO, LED1.cathode, R5.Pin_0, R5.Pin_1
  N9: Part2.GND, LED1.anode, LED2.anode, LED3.anode, LED4.anode, R1.Pin_0, R2.Pin_1, R3.Pin_1, R4.Pin_1
  N10: Part2.5V, S1.Pin_1, S1.Pin_2, S2.Pin_1, S2.Pin_2, S3.Pin_1, S3.Pin_2, S4.Pin_1, S4.Pin_2
